# Fritzing sketch CircuitoMotorGaraje (saved by Fritzing 0.9.3b)
breadboards: 1

parts:
  Componente1 = Arduino Uno (Rev3)
  U1 = G3VM-61E1 [package=g3vm-61e1]
  U2 = G3VM-61E1 [package=g3vm-61e1]
  S1 = Toggle Switch [package=THT]
  S2 = Pushbutton [package="[THT]"]
  R1 = Resistor [tolerance=±5% resistance=10k package=THT]
  U3 = atmega328 [package=dip]  # not connected

nets:
  N1: Componente1.D9_PWM, U1.P$1
  N2: Componente1.D10_PWM/SS, U2.P$1
  N3: Componente1.D11_PWM/MOSI, S1.L2
  N4: Componente1.D12/MISO, S1.L1
  N5: Componente1.GND, U1.P$3, U2.P$3, R1.Pin_1
  N6: Componente1.D2, S2.Pin_1, S2.Pin_2, R1.Pin_0
  N7: Componente1.5V, S1.COM, S2.Pin_3, S2.Pin_4

// code stored in the sketch: CircuitoMotorGaraje.ino

/**
  @file CircuitoMotorGaraje.ino
  @brief Controlador del motor de la puerta del garaje
  @author Pablo Rocamora pablojoserocamora@gmail.com
  @date 11/06/2018
*/

#include "CircuitoMotorGaraje.h"

#define MODO_DEBUG true



/**
   Metodo para comprobar si hemos pulsado el boton, retorna true si se ha pulsado y false en caso contrario
   Guarda el estado en el que esta.
*/
bool isClickButton() {
  bool clicked = false;
  int reading = digitalRead(CLICK_BUTTON);
  if (reading == HIGH && millis() - time > debounce) {
    time = millis();
    clicked = true;
  }

  return clicked;
  Serial.println(String(clicked));
}

/**
   Metodo para obtener el pin al que hay que aplicar voltaje para accionar el rele
*/
int getPinRelay() {
  int in = digitalRead(IS_CLOSE_DOOR);
  if (in == HIGH) {
    if (MODO_DEBUG)
      Serial.println("ABRIR");

    return RELAY_OPEN_DOOR;  //9
  }
  if (MODO_DEBUG)
    Serial.println("CERRAR");

  return RELAY_CLOSE_DOOR; //8
}

bool finCarrera(int relay) {
  int pin;
  if (relay == RELAY_OPEN_DOOR)
    pin = IS_OPEN_DOOR;
  else
    pin = IS_CLOSE_DOOR;

  int in = digitalRead(pin);

  if (MODO_DEBUG) {
    Serial.println(String(RELAY_OPEN_DOOR) + ": " + String(digitalRead(RELAY_OPEN_DOOR)));
    Serial.println(String(RELAY_CLOSE_DOOR) + ": " + String(digitalRead(RELAY_CLOSE_DOOR)));
    Serial.println(String(IS_CLOSE_DOOR) + ": " + String(digitalRead(IS_CLOSE_DOOR)));
    Serial.println(String(IS_OPEN_DOOR) + ": " + String(digitalRead(IS_OPEN_DOOR)));
    Serial.println(String(in == HIGH));
    Serial.println();
  }
  if (in == HIGH)
    return true;
  return false;
}


void pause(int pin) {
  digitalWrite(pin, LOW);
}

void play() {
  long inicio = millis();
  long fin = inicio + 10000; //tiempo maximo funcionando

  int relay =  getPinRelay();
  digitalWrite(relay, HIGH);
  Serial.println( "pin: " + String(relay));

  while (!finCarrera(relay)/* || millis() < fin*/) {
    Serial.println("play");

    if (isClickButton())
      pause(relay);
    delay(1000);
  }
  Serial.println("Termina play");
  digitalWrite(relay, LOW);
}



void setup() {
  if (MODO_DEBUG) {
    Serial.begin(115200);
    Serial.println("Inicio");
  }

  pinMode(RELAY_OPEN_DOOR, OUTPUT);
  pinMode(RELAY_CLOSE_DOOR, OUTPUT);
  pinMode(IS_OPEN_DOOR, INPUT);
  pinMode(IS_CLOSE_DOOR, INPUT);
  pinMode(CLICK_BUTTON, INPUT);
  pinMode(LED_OK, OUTPUT);

  digitalWrite(LED_OK, HIGH);
}

void loop() {
  if (isClickButton()) {
    play();
  }
  delay(100);
}
